# Fritzing sketch Avance (saved by Fritzing 0.9.3b)
breadboards: 1

parts:
  Part1 = Arduino Uno (Rev3)
  S1 = Pushbutton [package="[THT]"]
  S2 = Pushbutton [package="[THT]"]
  LED1 = LED - 5mm [color="White (4500K)" package="5 mm [THT]"]
  R1 = Resistor [tolerance=±5% resistance=220 package=THT]
  R2 = Resistor [tolerance=±5% resistance=220 package=THT]
  LED2 = LED - 5mm [color="Red (633nm)" package="5 mm [THT]"]
  R3 = Resistor [tolerance=±5% resistance=220 package=THT]
  LED3 = LED - 5mm [color="Blue (505nm)" package="5 mm [THT]"]
  R4 = Resistor [tolerance=±5% resistance=220 package=THT]
  LED4 = LED - 5mm [color="Yellow (592nm)" package="5 mm [THT]"]

nets:
  N1: Part1.D2, LED4.anode
  N2: Part1.D3_PWM, LED3.anode
  N3: Part1.D4, S1.Pin_3, S1.Pin_4
  N4: Part1.D5_PWM, S2.Pin_3, S2.Pin_4
  N5: Part1.D6_PWM, LED1.anode
  N6: Part1.D7, LED2.anode
  N7: Part1.5V, R1.Pin_1, R2.Pin_1, R3.Pin_1, R4.Pin_1
  N8: Part1.GND, S1.Pin_1, S1.Pin_2, S2.Pin_1, S2.Pin_2
  N9: LED1.cathode, R1.Pin_0
  N10: R2.Pin_0, LED2.cathode
  N11: R3.Pin_0, LED3.cathode
  N12: R4.Pin_0, LED4.cathode
